// Logisim project Lab1.circ as structural Verilog: 1 circuit, main circuit main
module main (
  input  B0,
  input  A1,
  input  A0,
  input  B1,
  input  C_in,
  input  [1:0] S1_S0,
  output D1,
  output D0,
  output C_out
);

  wire adder_1_cout, multiplexer_1_out, multiplexer_2_out, not_1_out, not_2_out;

  not not_1 (not_1_out, B0);
  not not_2 (not_2_out, B1);
  Multiplexer #(.enable("true"), .select(2)) multiplexer_1 (
    .in0(B0), .in1(not_1_out), .in2(1'b0), .in3(1'b1), .out(multiplexer_1_out), .sel(S1_S0));  // open: en
  Multiplexer #(.enable("true"), .select(2)) multiplexer_2 (
    .in0(B1), .in1(not_2_out), .in2(1'b0), .in3(1'b1), .out(multiplexer_2_out), .sel(S1_S0));  // open: en
  Adder #(.width(1)) adder_1 (.a(A0), .b(multiplexer_1_out), .out(D0), .cin(C_in), .cout(adder_1_cout));
  Adder #(.width(1)) adder_2 (.a(A1), .b(multiplexer_2_out), .out(D1), .cin(adder_1_cout), .cout(C_out));

  // Notes on the sheet:
  //   Design of 2-bit Arithmetic Unit 
  //   Group-9
endmodule
