// Logisim project lab2.1.circ as structural Verilog: 1 circuit, main circuit main
module main (
  input  UP,
  input  DOWN,
  input  Enable,
  input  RESET,
  output A,
  output B,
  output C,
  output D
);

  wire and_1_out, and_2_out, and_3_out, and_4_out, and_5_out, and_6_out, and_7_out, CLK_out, d_ff_1_qn,
       d_ff_2_qn, d_ff_3_qn, not_1_out, or_1_out, or_2_out, or_3_out, or_4_out, xor_1_out, xor_2_out,
       xor_3_out, xor_4_out;

  not not_1 (not_1_out, UP);
  or or_1 (or_1_out, UP, and_1_out);
  and and_1 (and_1_out, not_1_out, DOWN);
  and and_2 (and_2_out, and_1_out, d_ff_1_qn);
  and and_3 (and_3_out, and_2_out, d_ff_2_qn);
  and and_4 (and_4_out, and_3_out, d_ff_3_qn);
  and and_5 (and_5_out, UP, D);
  and and_6 (and_6_out, and_5_out, C);
  and and_7 (and_7_out, and_6_out, B);
  xor xor_1 (xor_1_out, D, or_1_out);
  or or_2 (or_2_out, and_5_out, and_2_out);
  or or_3 (or_3_out, and_3_out, and_6_out);
  or or_4 (or_4_out, and_7_out, and_4_out);
  xor xor_2 (xor_2_out, C, or_2_out);
  xor xor_3 (xor_3_out, B, or_3_out);
  xor xor_4 (xor_4_out, A, or_4_out);
  Clock CLK (.out(CLK_out));
  D_Flip_Flop d_ff_1 (.clk(CLK_out), .D(xor_1_out), .Q(D), .Qn(d_ff_1_qn), .preset(Enable), .reset(RESET));
  D_Flip_Flop d_ff_2 (.clk(CLK_out), .D(xor_2_out), .Q(C), .Qn(d_ff_2_qn), .preset(Enable), .reset(RESET));
  D_Flip_Flop d_ff_3 (.clk(CLK_out), .D(xor_3_out), .Q(B), .Qn(d_ff_3_qn), .preset(Enable), .reset(RESET));
  D_Flip_Flop d_ff_4 (.clk(CLK_out), .D(xor_4_out), .Q(A), .preset(Enable), .reset(RESET));  // open: Qn

  // Notes on the sheet:
  //   Fig : 4 bit binary Up-down Counter 
  //   Group - 9
  //   Riana Mahbub
endmodule
