// Logisim project lab2.2.circ as structural Verilog: 1 circuit, main circuit main
module main (
  input  UP,
  input  ENABLE,
  input  RESET,
  output A,
  output B,
  output C,
  output D,
  output E
);

  wire and_1_out, and_2_out, and_3_out, CLK_out;

  Clock CLK (.out(CLK_out));
  T_Flip_Flop t_ff_1 (.clk(CLK_out), .T(UP), .Q(E), .preset(ENABLE), .reset(RESET));  // open: Qn
  T_Flip_Flop t_ff_2 (.clk(CLK_out), .T(E), .Q(D), .preset(ENABLE), .reset(RESET));  // open: Qn
  T_Flip_Flop t_ff_3 (.clk(CLK_out), .T(and_1_out), .Q(C), .preset(ENABLE), .reset(RESET));  // open: Qn
  and and_1 (and_1_out, D, E);
  and and_2 (and_2_out, C, and_1_out);
  T_Flip_Flop t_ff_4 (.clk(CLK_out), .T(and_2_out), .Q(B), .preset(ENABLE), .reset(RESET));  // open: Qn
  and and_3 (and_3_out, B, and_2_out);
  T_Flip_Flop t_ff_5 (.clk(CLK_out), .T(and_3_out), .Q(A), .reset(RESET));  // open: Qn, preset

  // Notes on the sheet:
  //   Fig : 5 bit Up Counter Using T flip Flop
  //   Group 9 
  //   Riana Mahbub
endmodule
