// Logisim project lab2.3.circ as structural Verilog: 1 circuit, main circuit main
module main (
  input  ENABLE,
  input  RESET,
  output A,
  output B,
  output C,
  output D,
  output E
);

  wire CLK_out, d_ff_1_qn, d_ff_2_qn, d_ff_3_qn, d_ff_4_qn, d_ff_5_qn;

  Clock CLK (.out(CLK_out));
  D_Flip_Flop d_ff_1 (.clk(CLK_out), .D(d_ff_1_qn), .Q(E), .Qn(d_ff_1_qn), .preset(ENABLE), .reset(RESET));
  D_Flip_Flop d_ff_2 (.clk(E), .D(d_ff_2_qn), .Q(D), .Qn(d_ff_2_qn), .preset(ENABLE), .reset(RESET));
  D_Flip_Flop d_ff_3 (.clk(D), .D(d_ff_3_qn), .Q(C), .Qn(d_ff_3_qn), .preset(ENABLE), .reset(RESET));
  D_Flip_Flop d_ff_4 (.clk(C), .D(d_ff_4_qn), .Q(B), .Qn(d_ff_4_qn), .preset(ENABLE), .reset(RESET));
  D_Flip_Flop d_ff_5 (.clk(B), .D(d_ff_5_qn), .Q(A), .Qn(d_ff_5_qn), .preset(ENABLE), .reset(RESET));

  // Notes on the sheet:
  //   Fig : 5 bit Down counter using D flip flop
  //   Group 9
  //   Riana Mahbub
endmodule
