// Logisim project lab3qans.circ as structural Verilog: 1 circuit, main circuit main
module main (
  input  Reset,
  input  [1:0] in_2,
  input  SISL,
  input  SISR,
  input  I5,
  input  I4,
  input  I3,
  input  I2,
  input  I1,
  output A5,
  output A4,
  output A3,
  output A2,
  output A1
);

  wire Clk_out, multiplexer_1_out, multiplexer_2_out, multiplexer_3_out, multiplexer_4_out, multiplexer_5_out;

  Clock Clk (.out(Clk_out));
  Multiplexer #(.select(2)) multiplexer_1 (
    .in0(I5), .in1(A2), .in2(SISR), .in3(A5), .out(multiplexer_1_out), .sel(in_2));
  D_Flip_Flop d_ff_1 (.D(multiplexer_1_out), .clk(Clk_out), .Q(A5));  // open: Qn, preset, reset
  D_Flip_Flop d_ff_2 (.D(multiplexer_2_out), .clk(Clk_out), .Q(A4), .reset(Reset));  // open: Qn, preset
  Multiplexer #(.select(2)) multiplexer_2 (.in0(I4), .in1(A5), .in2(A2), .in3(A4), .out(multiplexer_2_out), .sel(in_2));
  D_Flip_Flop d_ff_3 (.D(multiplexer_3_out), .clk(Clk_out), .Q(A3), .reset(Reset));  // open: Qn, preset
  Multiplexer #(.select(2)) multiplexer_3 (.in0(I3), .in1(A4), .in2(A2), .in3(A3), .out(multiplexer_3_out), .sel(in_2));
  Multiplexer #(.select(2)) multiplexer_4 (.in0(I2), .in1(A3), .in2(A1), .in3(A2), .out(multiplexer_4_out), .sel(in_2));
  D_Flip_Flop d_ff_4 (.D(multiplexer_4_out), .clk(Clk_out), .Q(A2), .reset(Reset));  // open: Qn, preset
  Multiplexer #(.select(2)) multiplexer_5 (
    .in0(I1), .in1(SISL), .in2(A2), .in3(A1), .out(multiplexer_5_out), .sel(in_2));
  D_Flip_Flop d_ff_5 (.D(multiplexer_5_out), .clk(Clk_out), .Q(A1), .reset(Reset));  // open: Qn, preset

  // Notes on the sheet:
  //   Group -9
  //   Md. Faisal Sheikj
  //   ID : 2311554642
  //   Figure : 5 bit Universal Shift Register
endmodule
