// Logisim project lab4.2.circ as structural Verilog: 1 circuit, main circuit main
module main (
  input  A1,
  input  A2,
  input  A3,
  input  A4,
  input  B1,
  input  B2,
  input  B3,
  input  B4,
  input  in_9
);

  wire and_1_out;
  wire [2:0] and_2_out;
  wire [3:0] and_5_out;

  and and_1 (and_1_out, A1, B1);
  and and_2 (and_2_out[0], A1, B2);
  and and_3 (and_2_out[1], A1, B3);
  and and_4 (and_2_out[2], A1, B4);
  and and_5 (and_5_out[0], A2, B1);
  and and_6 (and_5_out[1], A2, B2);
  and and_7 (and_5_out[2], A2, B3);
  and and_8 (and_5_out[3], A2, B4);
  Adder #(.width(4)) adder_1 (.a({in_9, and_2_out}), .b(and_5_out));  // open: out, cin, cout
endmodule
