// Logisim project lab5.circ as structural Verilog: 2 circuits, main circuit main
module main (
  input  [15:0] in_1,
  input  in_2,
  input  in_3,
  input  [3:0] rs,
  input  [3:0] rt,
  input  [3:0] rd,
  input  [15:0] WriteData,
  input  CLK,
  input  Clear,
  output [15:0] out_10,
  output [15:0] ReadData1,
  output [15:0] ReadData2
);

  wire clock_1_out;

  Clock clock_1 (.out(clock_1_out));
  Register #(.width(16)) register_1 (.D(in_1), .Q(out_10), .clk(clock_1_out), .clr(in_2));  // open: en
  Register_16bit register_16bit_1 (
    .WriteData(WriteData), .WriteEnable(in_3), .ReadData1(ReadData1), .Read_Reg1(rs), .WriteRegister(rd),
    .ReadData2(ReadData2), .Read_Reg2(rt), .CLR(Clear), .CLK(CLK));
  Register_16bit register_16bit_2 ();  // open: WriteData, WriteEnable, ReadData1, Read_Reg1, WriteRegister, ReadData2, Read_Reg2, CLR, CLK

  // Notes on the sheet:
  //   Fig : Register File
  //   ID : 2312546642
endmodule

module Register_16bit (
  input  [15:0] WriteData,
  input  WriteEnable,
  input  [3:0] Read_Reg1,
  input  [3:0] WriteRegister,
  input  [3:0] Read_Reg2,
  input  CLR,
  input  CLK,
  output [15:0] ReadData1,
  output [15:0] ReadData2
);

  wire and_1_out, and_2_out, and_3_out, and_4_out, and_5_out, and_6_out, and_7_out, and_8_out, and_9_out,
       and_10_out, and_11_out, and_12_out, and_13_out, and_14_out, and_15_out, and_16_out, decoder_1_out0,
       decoder_1_out1, decoder_1_out2, decoder_1_out3, decoder_1_out4, decoder_1_out5, decoder_1_out6,
       decoder_1_out7, decoder_1_out8, decoder_1_out9, decoder_1_out10, decoder_1_out11, decoder_1_out12,
       decoder_1_out13, decoder_1_out14, decoder_1_out15;
  wire [15:0] register_1_q, register_2_q, register_4_q, register_5_q, register_6_q, register_7_q,
       register_8_q, register_9_q, register_10_q, register_11_q, register_12_q, register_13_q, register_14_q,
       register_15_q, RG1_q;

  Decoder #(.select(4)) decoder_1 (
    .out0(decoder_1_out0), .out1(decoder_1_out1), .out2(decoder_1_out2), .out3(decoder_1_out3),
    .out4(decoder_1_out4), .out5(decoder_1_out5), .out6(decoder_1_out6), .out7(decoder_1_out7),
    .out8(decoder_1_out8), .out9(decoder_1_out9), .out10(decoder_1_out10), .out11(decoder_1_out11),
    .out12(decoder_1_out12), .out13(decoder_1_out13), .out14(decoder_1_out14), .out15(decoder_1_out15),
    .sel(WriteRegister));  // open: en
  and and_1 (and_1_out, decoder_1_out0, WriteEnable);
  and and_2 (and_2_out, decoder_1_out1, WriteEnable);
  and and_3 (and_3_out, decoder_1_out2, WriteEnable);
  and and_4 (and_4_out, decoder_1_out3, WriteEnable);
  and and_5 (and_5_out, decoder_1_out4, WriteEnable);
  and and_6 (and_6_out, decoder_1_out5, WriteEnable);
  and and_7 (and_7_out, decoder_1_out6, WriteEnable);
  and and_8 (and_8_out, decoder_1_out7, WriteEnable);
  and and_9 (and_9_out, decoder_1_out8, WriteEnable);
  and and_10 (and_10_out, decoder_1_out9, WriteEnable);
  and and_11 (and_11_out, decoder_1_out10, WriteEnable);
  and and_12 (and_12_out, decoder_1_out11, WriteEnable);
  and and_13 (and_13_out, decoder_1_out12, WriteEnable);
  and and_14 (and_14_out, decoder_1_out13, WriteEnable);
  and and_15 (and_15_out, decoder_1_out14, WriteEnable);
  and and_16 (and_16_out, decoder_1_out15, WriteEnable);
  Register #(.width(16)) RG1 (.D(WriteData), .en(and_1_out), .Q(RG1_q), .clk(CLK), .clr(CLR));
  Register #(.width(16)) register_1 (.D(WriteData), .en(and_2_out), .Q(register_1_q), .clk(CLK), .clr(CLR));
  Register #(.width(16)) register_2 (.D(WriteData), .en(and_3_out), .Q(register_2_q), .clk(CLK), .clr(CLR));
  Register #(.width(16)) register_3 (.D(WriteData), .en(and_4_out), .Q(RG1_q), .clk(CLK), .clr(CLR));
  Register #(.width(16)) register_4 (.D(WriteData), .en(and_5_out), .Q(register_4_q), .clk(CLK), .clr(CLR));
  Register #(.width(16)) register_5 (.D(WriteData), .en(and_6_out), .Q(register_5_q), .clk(CLK), .clr(CLR));
  Register #(.width(16)) register_6 (.D(WriteData), .en(and_7_out), .Q(register_6_q), .clk(CLK), .clr(CLR));
  Register #(.width(16)) register_7 (.D(WriteData), .en(and_8_out), .Q(register_7_q), .clk(CLK), .clr(CLR));
  Register #(.width(16)) register_8 (.D(WriteData), .en(and_9_out), .Q(register_8_q), .clk(CLK), .clr(CLR));
  Register #(.width(16)) register_9 (.D(WriteData), .en(and_10_out), .Q(register_9_q), .clk(CLK), .clr(CLR));
  Register #(.width(16)) register_10 (.D(WriteData), .en(and_11_out), .Q(register_10_q), .clk(CLK), .clr(CLR));
  Register #(.width(16)) register_11 (.D(WriteData), .en(and_12_out), .Q(register_11_q), .clk(CLK), .clr(CLR));
  Register #(.width(16)) register_12 (.D(WriteData), .en(and_13_out), .Q(register_12_q), .clk(CLK), .clr(CLR));
  Register #(.width(16)) register_13 (.D(WriteData), .en(and_14_out), .Q(register_13_q), .clk(CLK), .clr(CLR));
  Register #(.width(16)) register_14 (.D(WriteData), .en(and_15_out), .Q(register_14_q), .clk(CLK), .clr(CLR));
  Register #(.width(16)) register_15 (.D(WriteData), .en(and_16_out), .Q(register_15_q), .clk(CLK), .clr(CLR));
  Multiplexer #(.select(4), .width(16)) multiplexer_1 (
    .in0(RG1_q), .in1(register_1_q), .in2(register_2_q), .in3(RG1_q), .in4(register_4_q), .in5(register_5_q),
    .in6(register_6_q), .in7(register_7_q), .in8(register_8_q), .in9(register_9_q), .in10(register_10_q),
    .in11(register_11_q), .in12(register_12_q), .in13(register_13_q), .in14(register_14_q),
    .in15(register_15_q), .out(ReadData1), .sel(Read_Reg1));  // open: en
  Multiplexer #(.select(4), .width(16)) multiplexer_2 (
    .in0(RG1_q), .in1(register_1_q), .in2(register_2_q), .in3(RG1_q), .in4(register_4_q), .in5(register_5_q),
    .in6(register_6_q), .in7(register_7_q), .in8(register_8_q), .in9(register_9_q), .in10(register_10_q),
    .in11(register_11_q), .in12(register_12_q), .in13(register_13_q), .in14(register_14_q),
    .in15(register_15_q), .out(ReadData2), .sel(Read_Reg2));  // open: en

  // Notes on the sheet:
  //   Fig : 
  //   16 Bit Register File
  //   SAKIB AHMED SHISHIR
  //   2312546642
  //   GROUP-9
endmodule
