// Logisim project lab6 12.03.2025 3.9.circ as structural Verilog: 3 circuits, main circuit alu
module alu (
  input  Cin,
  input  A,
  input  B,
  input  [1:0] Select,
  output Result,
  output Cout
);

  wire adder_1_out, and_1_out, multiplexer_1_out, not_1_out, or_1_out;

  not not_1 (not_1_out, B);
  and and_1 (and_1_out, A, B);
  or or_1 (or_1_out, A, B);
  Multiplexer #(.enable("true")) multiplexer_1 (
    .in0(B), .in1(not_1_out), .out(multiplexer_1_out), .sel(Select[0]));  // open: en
  Multiplexer #(.enable("true"), .select(2)) multiplexer_2 (
    .in0(and_1_out), .in1(or_1_out), .in2(adder_1_out), .in3(adder_1_out), .out(Result), .sel(Select));  // open: en
  Adder #(.width(1)) adder_1 (.a(A), .b(multiplexer_1_out), .out(adder_1_out), .cin(Cin), .cout(Cout));

  // Notes on the sheet:
  //   Fig : A one Bit ALU
  //   SAKIB AHMED SHISHIR
  //   2312546642
endmodule

module main (
  input  in_1,
  input  [15:0] in_2,
  input  [15:0] in_3,
  input  [1:0] in_4,
  output [15:0] out_5,
  output out_6,
  output out_7,
  output out_8
);

  ALU16bit alu16bit_1 (
    .Select(in_4), .B(in_3), .Cin(in_1), .A(in_2), .Cout(out_8), .Zero(out_6), .Result(out_5), .out_6(out_7));
  alu alu_1 ();  // open: A, B, Cin, Select, Result, Cout
  ALU16bit alu16bit_2 ();  // open: Select, B, Cin, A, Cout, Zero, Result, out_6
endmodule

module ALU16bit (
  input  Cin,
  input  [15:0] A,
  input  [15:0] B,
  input  [1:0] Select,
  output [15:0] Result,
  output out_6,
  output Zero,
  output Cout
);

  wire alu_1_cout, alu_2_cout, alu_3_cout, alu_4_cout, alu_5_cout, alu_6_cout, alu_7_cout, alu_8_cout,
       alu_9_cout, alu_10_cout, alu_11_cout, alu_12_cout, alu_13_cout, alu_14_cout, alu_15_cout;

  alu alu_1 (.A(A[0]), .B(B[0]), .Cin(Cin), .Select(Select), .Result(Result[0]), .Cout(alu_1_cout));
  alu alu_2 (.A(A[1]), .B(B[1]), .Cin(alu_1_cout), .Select(Select), .Result(Result[1]), .Cout(alu_2_cout));
  alu alu_3 (.A(A[2]), .B(B[2]), .Cin(alu_2_cout), .Select(Select), .Result(Result[2]), .Cout(alu_3_cout));
  alu alu_4 (.A(A[3]), .B(B[3]), .Cin(alu_3_cout), .Select(Select), .Result(Result[3]), .Cout(alu_4_cout));
  alu alu_5 (.A(A[4]), .B(B[4]), .Cin(alu_4_cout), .Select(Select), .Result(Result[4]), .Cout(alu_5_cout));
  alu alu_6 (.A(A[5]), .B(B[5]), .Cin(alu_5_cout), .Select(Select), .Result(Result[5]), .Cout(alu_6_cout));
  alu alu_7 (.A(A[6]), .B(B[6]), .Cin(alu_6_cout), .Select(Select), .Result(Result[6]), .Cout(alu_7_cout));
  alu alu_8 (.A(A[7]), .B(B[7]), .Cin(alu_7_cout), .Select(Select), .Result(Result[7]), .Cout(alu_8_cout));
  alu alu_9 (.A(A[8]), .B(B[8]), .Cin(alu_8_cout), .Select(Select), .Result(Result[8]), .Cout(alu_9_cout));
  alu alu_10 (.A(A[9]), .B(B[9]), .Cin(alu_9_cout), .Select(Select), .Result(Result[9]), .Cout(alu_10_cout));
  alu alu_11 (.A(A[10]), .B(B[10]), .Cin(alu_10_cout), .Select(Select), .Result(Result[10]), .Cout(alu_11_cout));
  alu alu_12 (.A(A[11]), .B(B[11]), .Cin(alu_11_cout), .Select(Select), .Result(Result[11]), .Cout(alu_12_cout));
  alu alu_13 (.A(A[12]), .B(B[12]), .Cin(alu_12_cout), .Select(Select), .Result(Result[12]), .Cout(alu_13_cout));
  alu alu_14 (.A(A[13]), .B(B[13]), .Cin(alu_13_cout), .Select(Select), .Result(Result[13]), .Cout(alu_14_cout));
  alu alu_15 (.A(A[14]), .B(B[14]), .Cin(alu_14_cout), .Select(Select), .Result(Result[14]), .Cout(alu_15_cout));
  alu alu_16 (.A(A[15]), .B(B[15]), .Cin(alu_15_cout), .Select(Select), .Result(Result[15]), .Cout(Cout));
  alu alu_17 ();  // open: A, B, Cin, Select, Result, Cout
  xor xor_1 (Zero, alu_15_cout, Cout);
  nor OverFlow (out_6, Result[0], Result[1], Result[2], Result[3], Result[4], Result[5], Result[6], Result[7], Result[8], Result[9], Result[10], Result[11], Result[12], Result[13], Result[14], Result[15]);
endmodule
