// Logisim project lab7.circ as structural Verilog: 6 circuits, main circuit main
module main (
  input  [15:0] in_1,
  input  in_2,
  input  [3:0] in_3,
  input  in_4,
  input  [3:0] in_5,
  input  [3:0] in_6,
  input  in_7,
  input  [15:0] in_8,
  input  in_9,
  input  in_10,
  input  [15:0] in_11,
  input  [15:0] in_12,
  input  [1:0] in_13,
  output [15:0] out_14,
  output [15:0] out_15,
  output [15:0] out_16,
  output [15:0] out_17,
  output out_18,
  output out_19,
  output out_20
);

  wire clock_1_out, clock_2_out;

  Clock clock_1 (.out(clock_1_out));
  Register #(.width(16)) register_1 (.D(in_1), .en(in_4), .Q(out_14), .clk(clock_1_out), .clr(in_7));
  ALU16bit alu16bit_1 (
    .Cin(in_9), .A(in_11), .B(in_12), .Select(in_13), .Result(out_17), .OverFlow(out_18), .Zero(out_19),
    .Cout(out_20));
  Clock clock_2 (.out(clock_2_out));
  ALU alu_1 ();  // open: Result, Cout, A, B, Cin, Select
  Register_16bit register_16bit_1 (
    .WriteData(in_8), .WriteEnable(in_2), .ReadData1(out_15), .Read_Reg1(in_3), .WriteRegister(in_6),
    .ReadData2(out_16), .Read_Reg2(in_5), .CLR(in_10), .CLK(clock_2_out));

  // Notes on the sheet:
  //   16 bit Register
  //   16 Bit ALU
  //   16 Bit RF
  //   Sakib Ahmed 
  //   ID : 2312546642
  //   1 Bit ALU
endmodule

module Register_16bit (
  input  [15:0] WriteData,
  input  WriteEnable,
  input  [3:0] Read_Reg1,
  input  [3:0] WriteRegister,
  input  [3:0] Read_Reg2,
  input  CLR,
  input  CLK,
  output [15:0] ReadData1,
  output [15:0] ReadData2
);

  wire and_1_out, and_2_out, and_3_out, and_4_out, and_5_out, and_6_out, and_7_out, and_8_out, and_9_out,
       and_10_out, and_11_out, and_12_out, and_13_out, and_14_out, and_15_out, and_16_out, decoder_1_out0,
       decoder_1_out1, decoder_1_out2, decoder_1_out3, decoder_1_out4, decoder_1_out5, decoder_1_out6,
       decoder_1_out7, decoder_1_out8, decoder_1_out9, decoder_1_out10, decoder_1_out11, decoder_1_out12,
       decoder_1_out13, decoder_1_out14, decoder_1_out15;
  wire [15:0] register_1_q, register_2_q, register_4_q, register_5_q, register_6_q, register_7_q,
       register_8_q, register_9_q, register_10_q, register_11_q, register_12_q, register_13_q, register_14_q,
       register_15_q, RG1_q;

  Decoder #(.select(4)) decoder_1 (
    .out0(decoder_1_out0), .out1(decoder_1_out1), .out2(decoder_1_out2), .out3(decoder_1_out3),
    .out4(decoder_1_out4), .out5(decoder_1_out5), .out6(decoder_1_out6), .out7(decoder_1_out7),
    .out8(decoder_1_out8), .out9(decoder_1_out9), .out10(decoder_1_out10), .out11(decoder_1_out11),
    .out12(decoder_1_out12), .out13(decoder_1_out13), .out14(decoder_1_out14), .out15(decoder_1_out15),
    .sel(WriteRegister));  // open: en
  and and_1 (and_1_out, decoder_1_out0, WriteEnable);
  and and_2 (and_2_out, decoder_1_out1, WriteEnable);
  and and_3 (and_3_out, decoder_1_out2, WriteEnable);
  and and_4 (and_4_out, decoder_1_out3, WriteEnable);
  and and_5 (and_5_out, decoder_1_out4, WriteEnable);
  and and_6 (and_6_out, decoder_1_out5, WriteEnable);
  and and_7 (and_7_out, decoder_1_out6, WriteEnable);
  and and_8 (and_8_out, decoder_1_out7, WriteEnable);
  and and_9 (and_9_out, decoder_1_out8, WriteEnable);
  and and_10 (and_10_out, decoder_1_out9, WriteEnable);
  and and_11 (and_11_out, decoder_1_out10, WriteEnable);
  and and_12 (and_12_out, decoder_1_out11, WriteEnable);
  and and_13 (and_13_out, decoder_1_out12, WriteEnable);
  and and_14 (and_14_out, decoder_1_out13, WriteEnable);
  and and_15 (and_15_out, decoder_1_out14, WriteEnable);
  and and_16 (and_16_out, decoder_1_out15, WriteEnable);
  Register #(.width(16)) RG1 (.D(WriteData), .en(and_1_out), .Q(RG1_q), .clk(CLK), .clr(CLR));
  Register #(.width(16)) register_1 (.D(WriteData), .en(and_2_out), .Q(register_1_q), .clk(CLK), .clr(CLR));
  Register #(.width(16)) register_2 (.D(WriteData), .en(and_3_out), .Q(register_2_q), .clk(CLK), .clr(CLR));
  Register #(.width(16)) register_3 (.D(WriteData), .en(and_4_out), .Q(RG1_q), .clk(CLK), .clr(CLR));
  Register #(.width(16)) register_4 (.D(WriteData), .en(and_5_out), .Q(register_4_q), .clk(CLK), .clr(CLR));
  Register #(.width(16)) register_5 (.D(WriteData), .en(and_6_out), .Q(register_5_q), .clk(CLK), .clr(CLR));
  Register #(.width(16)) register_6 (.D(WriteData), .en(and_7_out), .Q(register_6_q), .clk(CLK), .clr(CLR));
  Register #(.width(16)) register_7 (.D(WriteData), .en(and_8_out), .Q(register_7_q), .clk(CLK), .clr(CLR));
  Register #(.width(16)) register_8 (.D(WriteData), .en(and_9_out), .Q(register_8_q), .clk(CLK), .clr(CLR));
  Register #(.width(16)) register_9 (.D(WriteData), .en(and_10_out), .Q(register_9_q), .clk(CLK), .clr(CLR));
  Register #(.width(16)) register_10 (.D(WriteData), .en(and_11_out), .Q(register_10_q), .clk(CLK), .clr(CLR));
  Register #(.width(16)) register_11 (.D(WriteData), .en(and_12_out), .Q(register_11_q), .clk(CLK), .clr(CLR));
  Register #(.width(16)) register_12 (.D(WriteData), .en(and_13_out), .Q(register_12_q), .clk(CLK), .clr(CLR));
  Register #(.width(16)) register_13 (.D(WriteData), .en(and_14_out), .Q(register_13_q), .clk(CLK), .clr(CLR));
  Register #(.width(16)) register_14 (.D(WriteData), .en(and_15_out), .Q(register_14_q), .clk(CLK), .clr(CLR));
  Register #(.width(16)) register_15 (.D(WriteData), .en(and_16_out), .Q(register_15_q), .clk(CLK), .clr(CLR));
  Multiplexer #(.select(4), .width(16)) multiplexer_1 (
    .in0(RG1_q), .in1(register_1_q), .in2(register_2_q), .in3(RG1_q), .in4(register_4_q), .in5(register_5_q),
    .in6(register_6_q), .in7(register_7_q), .in8(register_8_q), .in9(register_9_q), .in10(register_10_q),
    .in11(register_11_q), .in12(register_12_q), .in13(register_13_q), .in14(register_14_q),
    .in15(register_15_q), .out(ReadData1), .sel(Read_Reg1));  // open: en
  Multiplexer #(.select(4), .width(16)) multiplexer_2 (
    .in0(RG1_q), .in1(register_1_q), .in2(register_2_q), .in3(RG1_q), .in4(register_4_q), .in5(register_5_q),
    .in6(register_6_q), .in7(register_7_q), .in8(register_8_q), .in9(register_9_q), .in10(register_10_q),
    .in11(register_11_q), .in12(register_12_q), .in13(register_13_q), .in14(register_14_q),
    .in15(register_15_q), .out(ReadData2), .sel(Read_Reg2));  // open: en

  // Notes on the sheet:
  //   Fig : 
  //   16 Bit Register File
  //   SAKIB AHMED SHISHIR
  //   2312546642
  //   GROUP-9
endmodule

module ALU (
  input  Cin,
  input  A,
  input  B,
  input  [1:0] Select,
  output Result,
  output Cout
);

  wire adder_1_out, and_1_out, multiplexer_1_out, not_1_out, or_1_out;

  not not_1 (not_1_out, B);
  and and_1 (and_1_out, A, B);
  or or_1 (or_1_out, A, B);
  Multiplexer multiplexer_1 (.in0(B), .in1(not_1_out), .out(multiplexer_1_out), .sel(Select[0]));  // open: en
  Multiplexer #(.select(2)) multiplexer_2 (
    .in0(and_1_out), .in1(or_1_out), .in2(adder_1_out), .in3(adder_1_out), .out(Result), .sel(Select));  // open: en
  Adder #(.width(1)) adder_1 (.a(A), .b(multiplexer_1_out), .out(adder_1_out), .cin(Cin), .cout(Cout));

  // Notes on the sheet:
  //   fig : A one Bit ALU
endmodule

module ALU16bit (
  input  Cin,
  input  [15:0] A,
  input  [15:0] B,
  input  [1:0] Select,
  output [15:0] Result,
  output OverFlow,
  output Zero,
  output Cout
);

  wire alu_1_cout, alu_2_cout, alu_3_cout, alu_4_cout, alu_5_cout, alu_6_cout, alu_7_cout, alu_8_cout,
       alu_9_cout, alu_10_cout, alu_11_cout, alu_12_cout, alu_13_cout, alu_14_cout, alu_15_cout;

  ALU alu_1 (.Result(Result[0]), .Cout(alu_1_cout), .A(A[0]), .B(B[0]), .Cin(Cin), .Select(Select));
  ALU alu_2 (.Result(Result[1]), .Cout(alu_2_cout), .A(A[1]), .B(B[1]), .Cin(alu_1_cout), .Select(Select));
  ALU alu_3 (.Result(Result[2]), .Cout(alu_3_cout), .A(A[2]), .B(B[2]), .Cin(alu_2_cout), .Select(Select));
  ALU alu_4 (.Result(Result[3]), .Cout(alu_4_cout), .A(A[3]), .B(B[3]), .Cin(alu_3_cout), .Select(Select));
  ALU alu_5 (.Result(Result[4]), .Cout(alu_5_cout), .A(A[4]), .B(B[4]), .Cin(alu_4_cout), .Select(Select));
  ALU alu_6 (.Result(Result[5]), .Cout(alu_6_cout), .A(A[5]), .B(B[5]), .Cin(alu_5_cout), .Select(Select));
  ALU alu_7 (.Result(Result[6]), .Cout(alu_7_cout), .A(A[6]), .B(B[6]), .Cin(alu_6_cout), .Select(Select));
  ALU alu_8 (.Result(Result[7]), .Cout(alu_8_cout), .A(A[7]), .B(B[7]), .Cin(alu_7_cout), .Select(Select));
  ALU alu_9 (.Result(Result[8]), .Cout(alu_9_cout), .A(A[8]), .B(B[8]), .Cin(alu_8_cout), .Select(Select));
  ALU alu_10 (.Result(Result[9]), .Cout(alu_10_cout), .A(A[9]), .B(B[9]), .Cin(alu_9_cout), .Select(Select));
  ALU alu_11 (.Result(Result[10]), .Cout(alu_11_cout), .A(A[10]), .B(B[10]), .Cin(alu_10_cout), .Select(Select));
  ALU alu_12 (.Result(Result[11]), .Cout(alu_12_cout), .A(A[11]), .B(B[11]), .Cin(alu_11_cout), .Select(Select));
  ALU alu_13 (.Result(Result[12]), .Cout(alu_13_cout), .A(A[12]), .B(B[12]), .Cin(alu_12_cout), .Select(Select));
  ALU alu_14 (.Result(Result[13]), .Cout(alu_14_cout), .A(A[13]), .B(B[13]), .Cin(alu_13_cout), .Select(Select));
  ALU alu_15 (.Result(Result[14]), .Cout(alu_15_cout), .A(A[14]), .B(B[14]), .Cin(alu_14_cout), .Select(Select));
  ALU alu_16 (.Result(Result[15]), .Cout(Cout), .A(A[15]), .B(B[15]), .Cin(alu_15_cout), .Select(Select));
  nor nor_1 (OverFlow, Result[0], Result[1], Result[2], Result[3], Result[4], Result[5], Result[6], Result[7], Result[8], Result[9], Result[10], Result[11], Result[12], Result[13], Result[14], Result[15]);
  xor xor_1 (Zero, alu_15_cout, Cout);
endmodule

module R_type_Datapath (
  input  Cin,
  input  WC,
  input  in_3,
  input  [1:0] Select,
  input  Clock,
  input  Clear,
  input  Clear_2,
  output Cout
);

  wire clock_1_out;
  wire [15:0] adder_1_out, alu16bit_1_result, PC_q, register_16bit_1_readdata1, register_16bit_1_readdata2,
       rom_1_data;

  Clock clock_1 (.out(clock_1_out));
  Register #(.width(16)) PC (.D(adder_1_out), .Q(PC_q), .clk(clock_1_out), .clr(Clear_2));  // open: en
  Adder #(.width(16)) adder_1 (.a(PC_q), .b(16'h1), .out(adder_1_out), .cin(in_3));  // open: cout
  ROM #(.addrWidth(16), .dataWidth(16)) rom_1 (.addr(PC_q), .data(rom_1_data));  // open: sel
  ALU16bit alu16bit_1 (
    .Cin(Cin), .A(register_16bit_1_readdata1), .B(register_16bit_1_readdata2), .Select(Select),
    .Result(alu16bit_1_result), .Cout(Cout));  // open: OverFlow, Zero
  Register_16bit register_16bit_1 (
    .WriteData(alu16bit_1_result), .WriteEnable(WC), .ReadData1(register_16bit_1_readdata1),
    .Read_Reg1(rom_1_data[11:8]), .WriteRegister(rom_1_data[3:0]), .ReadData2(register_16bit_1_readdata2),
    .Read_Reg2(rom_1_data[7:4]), .CLR(Clear), .CLK(Clock));

  // Notes on the sheet:
  //   ROM
  //   Fig : R type Datapath
  //   Opcode
  //   rs
  //   rt
  //   rd
  //   16 Bit RF
  //   16 Bit ALU
endmodule

module I_Type_Datapath (
  input  WC,
  input  Cin,
  input  in_3,
  input  Store_Signal,
  input  MemEn,
  input  Load,
  input  [1:0] Select,
  input  Clear,
  input  Clrear,
  input  Clear_2,
  output Cout
);

  wire clock_1_out;
  wire [15:0] adder_1_out, alu16bit_1_result, bit_extender_1_out, PC_q, ram_1_data,
       register_16bit_1_readdata1, register_16bit_1_readdata2, rom_1_data;

  Clock clock_1 (.out(clock_1_out));
  Register #(.width(16)) PC (.D(adder_1_out), .Q(PC_q), .clk(clock_1_out), .clr(Clrear));  // open: en
  Adder #(.width(16)) adder_1 (.a(PC_q), .b(16'h1), .out(adder_1_out), .cin(in_3));  // open: cout
  ROM #(.addrWidth(16), .dataWidth(16)) rom_1 (.addr(PC_q), .data(rom_1_data));  // open: sel
  assign bit_extender_1_out = {{12{1'b0}}, rom_1_data[3:0]};  // Bit_Extender bit_extender_1
  Register_16bit register_16bit_1 (
    .WriteData(ram_1_data), .WriteEnable(WC), .ReadData1(register_16bit_1_readdata1),
    .Read_Reg1(rom_1_data[11:8]), .WriteRegister(rom_1_data[7:4]), .ReadData2(register_16bit_1_readdata2),
    .Read_Reg2(rom_1_data[7:4]), .CLR(Clear_2), .CLK(clock_1_out));
  ALU16bit alu16bit_1 (
    .Cin(Cin), .A(register_16bit_1_readdata1), .B(bit_extender_1_out), .Select(Select),
    .Result(alu16bit_1_result), .Cout(Cout));  // open: OverFlow, Zero
  RAM #(.addrWidth(16), .dataWidth(16), .bus("separate")) ram_1 (
    .addr(alu16bit_1_result), .din(register_16bit_1_readdata2), .data(ram_1_data), .str(Store_Signal),
    .sel(MemEn), .clk(clock_1_out), .ld(Load), .clr(Clear));

  // Notes on the sheet:
  //   ROM
  //   contents of rom_1 (hex, n*v repeats v):
  //   123
  //   Immediate
  //   opcode
  //   Fig : I type Datapath
  //   rt
  //   rs
  //   rs
  //   rt
  //   rd
  //   16 bit RF
  //   16bit ALU
  //   RAM 
endmodule
