// Logisim project lab8.1.circ as structural Verilog: 1 circuit, main circuit main
module main (
  input  T,
  input  D,
  output out_3,
  output out_4
);

  wire Clk_out, clock_1_out, not_1_out;

  J_K_Flip_Flop j_k_ff_1 (.J(T), .K(T), .clk(Clk_out), .Q(out_3));  // open: Qn, preset, reset
  Clock Clk (.out(Clk_out));
  not not_1 (not_1_out, D);
  J_K_Flip_Flop j_k_ff_2 (.J(D), .K(not_1_out), .clk(clock_1_out), .Q(out_4));  // open: Qn, preset, reset
  Clock clock_1 (.out(clock_1_out));

  // Notes on the sheet:
  //   Clk
endmodule
