// Logisim project lab8.2.circ as structural Verilog: 1 circuit, main circuit main
module main (
  input  Input,
  input  in_2,
  output Qo,
  output Q1,
  output Q2,
  output Q3
);

  wire n7474_1_pin3;

  _7474 u_7474_1 (
    .pin1(in_2), .pin2(Input), .pin3(n7474_1_pin3), .pin4(in_2), .pin5(Qo), .pin13(in_2), .pin12(Qo),
    .pin11(n7474_1_pin3), .pin10(in_2), .pin9(Q1));  // open: pin6, pin8
  _7474 u_7474_2 (
    .pin1(in_2), .pin2(Q1), .pin3(n7474_1_pin3), .pin4(in_2), .pin5(Q2), .pin13(in_2), .pin12(Q2),
    .pin11(n7474_1_pin3), .pin10(in_2), .pin9(Q3));  // open: pin6, pin8
  Clock clock_1 (.out(n7474_1_pin3));

  // Notes on the sheet:
  //   Serial
  //   Serial Output
  //   Clock Pulse
  //   Figure : Shift Register
  //   Sakib Ahmed Shishir
  //   2312546642
  //   D flip-Flop
endmodule
