// Logisim project lab8.3.circ as structural Verilog: 1 circuit, main circuit main
module main (
  input  D,
  output out_2
);

  wire clock_1_out, not_1_out;

  not not_1 (not_1_out, D);
  J_K_Flip_Flop j_k_ff_1 (.J(D), .K(not_1_out), .clk(clock_1_out), .Q(out_2));  // open: Qn, preset, reset
  Clock clock_1 (.out(clock_1_out));

  // Notes on the sheet:
  //   D Flip Flop using a J-K flip flop
  //   Clk
endmodule
