// Logisim project mos1.circ as structural Verilog: 2 circuits, main circuit main
module main (
  input  in_1,
  input  in_2,
  input  in_3
);

  wire cmos_1_a, cmos_1_b, cmos_1_d, cmos_1_e, cmos_1_f, cmos_1_g, cmos_1_out_6;

  CMOS cmos_1 (
    .in_1(in_3), .in_2(in_2), .C(in_1), .a(cmos_1_a), .b(cmos_1_b), .out_6(cmos_1_out_6), .d(cmos_1_d),
    .e(cmos_1_e), .f(cmos_1_f), .g(cmos_1_g));
  _7_Segment_Display u_7_segment_display_1 (
    .g(cmos_1_g), .f(cmos_1_f), .a(cmos_1_b), .b(cmos_1_a), .e(cmos_1_e), .d(cmos_1_d), .c(cmos_1_out_6));  // open: dp
endmodule

module CMOS (
  input  in_1,
  input  in_2,
  input  C,
  output a,
  output b,
  output out_6,
  output d,
  output e,
  output f,
  output g
);

  wire and_1_out, and_2_out, and_3_out, and_4_out, and_5_out, and_6_out, and_7_out, and_8_out, and_9_out,
       and_10_out, not_1_out, not_2_out, not_3_out;

  not not_1 (not_1_out, in_1);
  not not_2 (not_2_out, in_2);
  not not_3 (not_3_out, C);
  and and_1 (and_1_out, not_1_out, C);
  or or_1 (a, and_1_out, and_2_out);
  and and_2 (and_2_out, not_2_out, not_3_out);
  or or_2 (b, not_1_out, C);
  and and_3 (and_3_out, not_2_out, C);
  and and_4 (and_4_out, in_2, not_3_out);
  or or_3 (out_6, and_3_out, and_4_out, in_1);
  and and_5 (and_5_out, not_1_out, C);
  and and_6 (and_6_out, in_1, not_3_out);
  or or_4 (d, and_5_out, and_6_out, and_7_out);
  and and_7 (and_7_out, not_1_out, not_2_out);
  and and_8 (and_8_out, not_1_out, not_2_out, not_3_out);
  and and_9 (and_9_out, in_2, C);
  or or_5 (e, and_8_out, and_9_out, and_10_out);
  and and_10 (and_10_out, in_1, in_2);
  or or_6 (g, not_2_out, C, in_1);

  assign f = in_1;
endmodule
