// Logisim project operation1.circ as structural Verilog: 1 circuit, main circuit main
module main (
  input  A,
  input  B,
  input  C,
  output I1___A_prime_C,
  output F__I1__I2__I3,
  output I2___AB_prime,
  output I3___BC
);

  wire not_1_out, not_2_out, or_1_out;

  not not_1 (not_1_out, A);
  not not_2 (not_2_out, B);
  and and_1 (I1___A_prime_C, not_1_out, C);
  and and_2 (I2___AB_prime, A, not_2_out);
  and and_3 (I3___BC, B, C);
  or or_1 (or_1_out, I1___A_prime_C, I2___AB_prime);
  or or_2 (F__I1__I2__I3, or_1_out, I3___BC);

  // Notes on the sheet:
  //   Figure D.3 Circuit Diagram for the Boolean function F
  //   Sakib Ahmed Shishir 
  //   2312546642
endmodule
