// Logisim project operation5.circ as structural Verilog: 1 circuit, main circuit main
module main (
  input  A,
  input  B,
  input  C,
  output AC_BC_prime
);

  wire nor_1_out, nor_2_out, nor_3_out, nor_4_out, nor_5_out, nor_6_out;

  nor nor_1 (nor_1_out, A, A);
  nor nor_2 (nor_2_out, C, C);
  nor nor_3 (nor_3_out, B, B);
  nor nor_4 (nor_4_out, nor_1_out, nor_2_out);
  nor nor_5 (nor_5_out, nor_3_out, C);
  nor nor_6 (nor_6_out, nor_4_out, nor_5_out);
  nor nor_7 (AC_BC_prime, nor_6_out, nor_6_out);

  // Notes on the sheet:
  //   C'
  //   B'
  //   (A+A)'=A'
  //   Figure B2 : A Combinational Circuit using NOR Gates
  //   (A'+C')'=AC
  //   (AC+BC')'
  //   (B'+C)'=BC'
  //   Md. Tarek Tahman Chowdhury Oishajra 
  //   ID :  1822172642
endmodule
