// Logisim project operation6.1.1.circ as structural Verilog: 1 circuit, main circuit main
module main (
  input  A,
  input  B,
  input  C,
  input  D,
  output out_5,
  output out_6,
  output Y__C_prime_D_prime_CD,
  output out_8
);

  wire nor_1_out, nor_2_out, nor_3_out, nor_4_out, nor_5_out, nor_6_out, nor_7_out, nor_8_out, nor_9_out,
       nor_10_out, nor_11_out, nor_12_out, nor_13_out, nor_14_out, nor_16_out, nor_17_out, nor_18_out,
       nor_19_out, nor_20_out, nor_21_out, nor_22_out, nor_23_out, nor_24_out, nor_25_out, nor_28_out;

  nor nor_1 (nor_1_out, B, B);
  nor nor_2 (nor_2_out, C, C);
  nor nor_3 (nor_3_out, B, B);
  nor nor_4 (nor_4_out, D, D);
  nor nor_5 (nor_5_out, B, B);
  nor nor_6 (nor_6_out, C, C);
  nor nor_7 (nor_7_out, B, D);
  nor nor_8 (nor_8_out, C, C);
  nor nor_9 (nor_9_out, D, D);
  nor nor_10 (nor_10_out, nor_1_out, nor_2_out);
  nor nor_11 (nor_11_out, nor_3_out, nor_4_out);
  nor nor_12 (nor_12_out, nor_6_out, nor_6_out);
  nor nor_13 (nor_13_out, D, D);
  nor nor_14 (nor_14_out, B, B);
  nor nor_15 (out_8, D, D);
  nor nor_16 (nor_16_out, A, nor_10_out);
  nor nor_17 (nor_17_out, B, nor_13_out);
  nor nor_18 (nor_18_out, nor_14_out, C);
  nor nor_19 (nor_19_out, nor_8_out, nor_9_out);
  nor nor_20 (nor_20_out, nor_16_out, nor_16_out);
  nor nor_21 (nor_21_out, nor_5_out, nor_12_out);
  nor nor_22 (nor_22_out, nor_17_out, nor_18_out);
  nor nor_23 (nor_23_out, nor_7_out, nor_19_out);
  nor nor_24 (nor_24_out, nor_20_out, nor_11_out);
  nor nor_25 (nor_25_out, nor_22_out, nor_22_out);
  nor nor_26 (Y__C_prime_D_prime_CD, nor_23_out, nor_23_out);
  nor nor_27 (out_5, nor_24_out, nor_24_out);
  nor nor_28 (nor_28_out, nor_21_out, nor_25_out);
  nor nor_29 (out_6, nor_28_out, nor_28_out);

  // Notes on the sheet:
  //   B'
  //   C'
  //   B'
  //   D'
  //   (C+D)'
  //   C
  //   (B'+C')' =BC
  //   B'
  //   (C+D)
  //   D'
  //   B'
  //   (C+D)' =C'D'
  //   C'
  //   D'
  //   (A+BC)'
  //   (B'+D')' =BD
  //   (B+D')'
  //   (B'+C)'
  //   BC'D'
  //   (BD'+B'C)'
  //   (C'D'+CD)'
  //   (C'+D')' = CD
  //   Z = D'
  //   Figure E3 : Minimal Universal gate implementation of BCD to Excess-3 Converter
  //   A+BC
  //   (A+BC+BD)'
  //   (BD'+B'C)
  //   W= A+BC+BD
  //   (BC'D'+BD'+B'C)'
  //   Nafia Haque Muskan
  //   ID : 2311677042
  //   X= (BC'D'+BD'+B'C)
endmodule
